// Logisim project harness.circ as structural Verilog: 1 circuit, main circuit main
module main (
  output halt,
  output LED0,
  output LED2,
  output S0,
  output LED1,
  output S1,
  output LED3
);

  wire clock_1_out;
  wire [1:0] counter_1_q;

  Clock clock_1 (.out(clock_1_out));
  ROM #(.addrWidth(2), .dataWidth(2)) rom_1 (.addr(counter_1_q), .data({S1, S0}));
  Counter #(.max('h3), .width(2)) counter_1 (
    .clr(1'b0), .clk(clock_1_out), .carry(halt), .Q(counter_1_q));  // open: load, up, count, D
  // m00_e01_main m00_e01_main_1: pin names not known; wires that end beside it: S0, S1, LED0, LED2, LED1, LED3

  // Notes on the sheet:
  //   contents of rom_1 (hex, n*v repeats v):
  //   0 1 2 3
endmodule
