// Logisim project starter.circ as structural Verilog: 1 circuit, main circuit m00_e01_main
module m00_e01_main (
  input  S0,
  input  S1,
  output LED0,
  output LED2,
  output LED1,
  output LED3
);

  LED LED_0 (.in(LED0));
  LED LED_2 (.in(LED2));
  LED LED_1 (.in(LED1));
  LED LED_3 (.in(LED3));
endmodule
