// Logisim project harness.circ as structural Verilog: 1 circuit, main circuit main
module main (
  output halt,
  output ALARM,
  output DOOR,
  output WINDOW,
  output FIRE
);

  wire clock_1_out;
  wire [2:0] counter_1_q;

  Clock clock_1 (.out(clock_1_out));
  ROM #(.addrWidth(3), .dataWidth(3)) rom_1 (.addr(counter_1_q), .data({FIRE, WINDOW, DOOR}));
  Counter #(.max('h7), .width(3)) counter_1 (
    .clr(1'b0), .clk(clock_1_out), .carry(halt), .Q(counter_1_q));  // open: load, up, count, D
  // m00_e02_main m00_e02_main_1: pin names not known; wires that end beside it: DOOR, WINDOW, FIRE, ALARM

  // Notes on the sheet:
  //   contents of rom_1 (hex, n*v repeats v):
  //   0 1 2 3 4 5 6 7
endmodule
