// Logisim project starter.circ as structural Verilog: 1 circuit, main circuit m00_e02_main
module m00_e02_main (
  input  DOOR,
  input  WINDOW,
  input  FIRE,
  output ALARM
);

  // Buzzer buzzer_1: pin names not known; wires that end beside it: ALARM, ALARM
endmodule
