// Logisim project harness.circ as structural Verilog: 1 circuit, main circuit main
module main (
  output halt,
  output A,
  output B,
  output RESULT,
  output C
);

  wire clock_1_out;
  wire [2:0] counter_1_q;

  Clock clock_1 (.out(clock_1_out));
  ROM #(.addrWidth(3), .dataWidth(3)) rom_1 (.addr(counter_1_q), .data({C, B, A}));
  Counter #(.max('h7), .width(3)) counter_1 (
    .clr(1'b0), .clk(clock_1_out), .carry(halt), .Q(counter_1_q));  // open: load, up, count, D
  // m00_ex05_main m00_ex05_main_1: pin names not known; wires that end beside it: A, B, C, RESULT

  // Notes on the sheet:
  //   contents of rom_1 (hex, n*v repeats v):
  //   0 1 2 3 4 5 6 7
endmodule
