// Logisim project starter.circ as structural Verilog: 1 circuit, main circuit m00_ex06_main
module m00_ex06_main (
  input  A,
  input  B,
  input  C,
  input  D,
  output RESULT
);
endmodule
