// Logisim project harness.circ as structural Verilog: 1 circuit, main circuit main
module main (
  output halt,
  output [3:0] A,
  output GT,
  output LT,
  output EQ,
  output LE,
  output GE,
  output [3:0] B
);

  wire clock_1_out;
  wire [7:0] counter_1_q;

  Clock clock_1 (.out(clock_1_out));
  ROM #(.dataWidth(4)) rom_1 (.addr(counter_1_q), .data(A));
  ROM #(.dataWidth(4)) rom_2 (.addr(counter_1_q), .data(B));
  Counter counter_1 (.clr(1'b0), .clk(clock_1_out), .carry(halt), .Q(counter_1_q));  // open: load, up, count, D
  // m00_ex07_main m00_ex07_main_1: pin names not known; wires that end beside it: A, B, GT, LT, EQ, LE, GE

  // Notes on the sheet:
  //   contents of rom_1 (hex, n*v repeats v):
  //   16*0 16*1 16*2 16*3 16*4 16*5 16*6 16*7 16*8 16*9 16*a 16*b 16*c 16*d 16*e 16*f
  //   contents of rom_2 (hex, n*v repeats v):
  //   0 1 2 3 4 5 6 7 8 9 a b c d e f 0 1 2 3 4 5 6 7 8 9 a b c d e f 0 1 2 3 4 5 6 7 8 9 a b c d e f 0 1
  //   2 3 4 5 6 7 8 9 a b c d e f 0 1 2 3 4 5 6 7 8 9 a b c d e f 0 1 2 3 4 5 6 7 8 9 a b c d e f 0 1 2 3
  //   4 5 6 7 8 9 a b c d e f 0 1 2 3 4 5 6 7 8 9 a b c d e f 0 1 2 3 4 5 6 7 8 9 a b c d e f 0 1 2 3 4 5
  //   6 7 8 9 a b c d e f 0 1 2 3 4 5 6 7 8 9 a b c d e f 0 1 2 3 4 5 6 7 8 9 a b c d e f 0 1 2 3 4 5 6 7
  //   8 9 a b c d e f 0 1 2 3 4 5 6 7 8 9 a b c d e f 0 1 2 3 4 5 6 7 8 9 a b c d e f 0 1 2 3 4 5 6 7 8 9
  //   a b c d e f
endmodule
