// Logisim project harness.circ as structural Verilog: 1 circuit, main circuit main
module main (
  output SEG_A,
  output SEG_B,
  output halt,
  output SEG_C,
  output SEG_D,
  output [3:0] DATA,
  output SEG_E,
  output SEG_F,
  output SEG_G
);

  wire clock_1_out;

  Clock clock_1 (.out(clock_1_out));
  Counter #(.max('hf), .width(4)) counter_1 (
    .clr(1'b0), .clk(clock_1_out), .carry(halt), .Q(DATA));  // open: load, up, count, D
  // m00_ex08_main m00_ex08_main_1: pin names not known; wires that end beside it: DATA, SEG_A, SEG_B, SEG_C, SEG_D, SEG_E, SEG_F, SEG_G
endmodule
