// Logisim project starter.circ as structural Verilog: 1 circuit, main circuit m00_ex08_main
module m00_ex08_main (
  input  [3:0] DATA,
  output SEG_A,
  output SEG_B,
  output SEG_C,
  output SEG_D,
  output SEG_E,
  output SEG_F,
  output SEG_G
);

  _7_Segment_Display u_7_segment_display_1 (
    .g(SEG_G), .f(SEG_F), .a(SEG_A), .b(SEG_B), .e(SEG_E), .d(SEG_D), .c(SEG_C));  // open: dp
endmodule
